// Digital circuit Circuito.dig as structural Verilog
module Circuito (
  input  B3,
  input  B2,
  input  B1,
  input  B0,
  input  A3,
  input  A2,
  input  A1,
  input  A0,
  input  O0,
  input  O1,
  input  A4,
  input  A5,
  input  B4,
  input  B5,
  output s7,
  output s6,
  output s5,
  output s4,
  output s3,
  output s2,
  output s1,
  output s0,
  output F
);

  wire comparator_1_s0, comparator_1_s1, comparator_1_s2, comparator_1_s3, comparator_1_s4, comparator_1_s5,
       multiplicador_1_c0, multiplicador_1_c1, multiplicador_1_c2, multiplicador_1_c3, multiplicador_1_c4,
       multiplicador_1_c5, multiplicador_1_c6, multiplicador_1_c7, multiplicador_1_f, somador_1_f,
       somador_1_s0, somador_1_s1, somador_1_s2, somador_1_s3, somador_1_s4, somador_1_s5, subtractor_1_f,
       subtractor_1_s0, subtractor_1_s1, subtractor_1_s2, subtractor_1_s3, subtractor_1_s4, subtractor_1_s5;

  Multiplicador multiplicador_1 (
    .A0(A0), .A1(A1), .A2(A2), .A3(A3), .A4(A4), .A5(A5), .B5(B5), .B4(B4), .B3(B3), .B2(B2), .B1(B1),
    .B0(B0), .C0(multiplicador_1_c0), .C1(multiplicador_1_c1), .C2(multiplicador_1_c2),
    .C3(multiplicador_1_c3), .C4(multiplicador_1_c4), .C5(multiplicador_1_c5), .C6(multiplicador_1_c6),
    .C7(multiplicador_1_c7), .F(multiplicador_1_f));
  Comparator comparator_1 (
    .A0(A0), .A1(A1), .A2(A2), .A3(A3), .A4(A4), .A5(A5), .B5(B5), .B4(B4), .B3(B3), .B2(B2), .B1(B1),
    .B0(B0), .s0(comparator_1_s0), .s1(comparator_1_s1), .s2(comparator_1_s2), .s3(comparator_1_s3),
    .s4(comparator_1_s4), .s5(comparator_1_s5));
  Mux_de_6_bits mux_de_6_bits_1 (
    .F_Som(somador_1_f), ._00(O0), ._01(O1), .S0_Som(somador_1_s0), .S1_Som(somador_1_s1),
    .S2_Som(somador_1_s2), .S3_Som(somador_1_s3), .S4_Som(somador_1_s4), .S5_Som(somador_1_s5),
    .S0_Sub(subtractor_1_s0), .S1_Sub(subtractor_1_s1), .S2_Sub(subtractor_1_s2), .S3_Sub(subtractor_1_s3),
    .S4_Sub(subtractor_1_s4), .S5_Sub(subtractor_1_s5), .F_Sub(subtractor_1_f), .S0_Com(comparator_1_s0),
    .S1_Com(comparator_1_s1), .S2_Com(comparator_1_s2), .S3_Com(comparator_1_s3), .S4_Com(comparator_1_s4),
    .S5_Com(comparator_1_s5), .S0_Mul(multiplicador_1_c0), .S1_Mul(multiplicador_1_c1),
    .S2_Mul(multiplicador_1_c2), .S3_Mul(multiplicador_1_c3), .S4_Mul(multiplicador_1_c4),
    .S5_Mul(multiplicador_1_c5), .S6_Mul(multiplicador_1_c6), .S7_Mul(multiplicador_1_c7),
    .F_Mul(multiplicador_1_f), .S0(s0), .S1(s1), .S2(s2), .S3(s3), .S4(s4), .S5(s5), .S6(s6), .S7(s7), .F(F));
  Subtractor subtractor_1 (
    .A5(A5), .A4(A4), .A3(A3), .A2(A2), .A1(A1), .A0(A0), .B5(B5), .B4(B4), .B3(B3), .B2(B2), .B1(B1),
    .B0(B0), .s0(subtractor_1_s0), .s1(subtractor_1_s1), .s2(subtractor_1_s2), .s3(subtractor_1_s3),
    .s4(subtractor_1_s4), .s5(subtractor_1_s5), .F(subtractor_1_f));
  Somador somador_1 (
    .A5(A5), .A4(A4), .A3(A3), .A2(A2), .A1(A1), .A0(A0), .B5(B5), .B4(B4), .B3(B3), .B2(B2), .B1(B1),
    .B0(B0), .F(somador_1_f), .s0(somador_1_s0), .s1(somador_1_s1), .s2(somador_1_s2), .s3(somador_1_s3),
    .s4(somador_1_s4), .s5(somador_1_s5));
endmodule
