// Digital circuit Comparador SImples,,.dig as structural Verilog
module Comparador_SImples (
  input  S0,
  input  S1,
  input  S2,
  input  S3,
  input  S4,
  input  S5,
  output _0,
  output _1,
  output _2,
  output _3,
  output _4,
  output _5
);

  wire and_1_out, and_2_out, and_3_out, and_4_out;

  and and_1 (and_1_out, ~S0, ~S1);  // And
  and and_2 (and_2_out, ~S2, ~S3);  // And
  and and_3 (and_3_out, ~S4, ~S5);  // And
  and and_4 (and_4_out, and_1_out, and_2_out);
  and and_5 (_0, and_4_out, and_3_out);
  and and_6 (_1, ~S5, S5);  // And
  and and_7 (_2, ~S5, S5);  // And
  and and_8 (_3, ~S5, S5);  // And
  and and_9 (_4, ~S5, S5);  // And
  and and_10 (_5, ~S5, S5);  // And
endmodule
