// Digital circuit Comparator.dig as structural Verilog
module Comparator (
  input  A0,
  input  A1,
  input  A2,
  input  A3,
  input  A4,
  input  A5,
  input  B5,
  input  B4,
  input  B3,
  input  B2,
  input  B1,
  input  B0,
  output s0,
  output s1,
  output s2,
  output s3,
  output s4,
  output s5
);

  wire complemento_de_2_1_s0, complemento_de_2_1_s1, complemento_de_2_1_s2, complemento_de_2_1_s3,
       complemento_de_2_1_s4, complemento_de_2_1_s5, full_adder_1_cout, full_adder_1_s, full_adder_2_cout,
       full_adder_2_s, full_adder_3_cout, full_adder_3_s, full_adder_4_cout, full_adder_4_s, full_adder_5_s,
       half_adder_1_cout, half_adder_1_s;

  Complemento_de_2 complemento_de_2_1 (
    .B0(B0), .B1(B1), .B2(B2), .B3(B3), .B4(B4), .B5(B5), .S0(complemento_de_2_1_s0),
    .S1(complemento_de_2_1_s1), .S2(complemento_de_2_1_s2), .S3(complemento_de_2_1_s3),
    .S4(complemento_de_2_1_s4), .S5(complemento_de_2_1_s5));
  Half_Adder half_adder_1 (.A(A0), .B(complemento_de_2_1_s0), .S(half_adder_1_s), .Cout(half_adder_1_cout));
  Full_Adder full_adder_1 (
    .A(A1), .B(complemento_de_2_1_s1), .Cin(half_adder_1_cout), .S(full_adder_1_s), .Cout(full_adder_1_cout));
  Full_Adder full_adder_2 (
    .A(A2), .B(complemento_de_2_1_s2), .Cin(full_adder_1_cout), .S(full_adder_2_s), .Cout(full_adder_2_cout));
  Full_Adder full_adder_3 (
    .A(A3), .B(complemento_de_2_1_s3), .Cin(full_adder_2_cout), .S(full_adder_3_s), .Cout(full_adder_3_cout));
  Full_Adder full_adder_4 (
    .A(A4), .B(complemento_de_2_1_s4), .Cin(full_adder_3_cout), .S(full_adder_4_s), .Cout(full_adder_4_cout));
  Full_Adder full_adder_5 (
    .A(A5), .B(complemento_de_2_1_s5), .Cin(full_adder_4_cout), .S(full_adder_5_s));  // open: Cout
  Comparador_SImples comparador_simples_1 (
    .S0(half_adder_1_s), .S1(full_adder_1_s), .S2(full_adder_2_s), .S3(full_adder_3_s), .S4(full_adder_4_s),
    .S5(full_adder_5_s), ._0(s0), ._1(s1), ._2(s2), ._3(s3), ._4(s4), ._5(s5));
endmodule
