// Digital circuit Complemento de 2.dig as structural Verilog
module Complemento_de_2 (
  input  B0,
  input  B1,
  input  B2,
  input  B3,
  input  B4,
  input  B5,
  output S0,
  output S1,
  output S2,
  output S3,
  output S4,
  output S5
);

  wire not_1_out, not_2_out, not_3_out, not_4_out, not_5_out, not_6_out;

  not not_1 (not_1_out, B0);
  not not_2 (not_2_out, B1);
  not not_3 (not_3_out, B2);
  not not_4 (not_4_out, B3);
  not not_5 (not_5_out, B4);
  not not_6 (not_6_out, B5);
  Somador_do_Complemento_de_2 somador_do_complemento_de_2_1 (
    .B0(not_1_out), .B1(not_2_out), .B2(not_3_out), .B3(not_4_out), .B4(not_5_out), .B5(not_6_out), .s0(S0),
    .s1(S1), .s2(S2), .s3(S3), .s4(S4), .s5(S5));
endmodule
