// Digital circuit Full Adder.dig as structural Verilog
module Full_Adder (
  input  A,
  input  B,
  input  Cin,
  output S,
  output Cout
);

  wire and_1_out, and_2_out, and_3_out, xor_1_out;

  xor xor_1 (xor_1_out, B, Cin);
  and and_1 (and_1_out, Cin, B);
  and and_2 (and_2_out, Cin, A);
  and and_3 (and_3_out, B, A);
  xor xor_2 (S, A, xor_1_out);
  or or_1 (Cout, and_1_out, and_2_out, and_3_out);
endmodule
