// Digital circuit Full Comparator.dig as structural Verilog
module Full_Comparator (
  input  E0,
  input  E1,
  input  E2,
  input  E3,
  input  E4,
  input  E5,
  output S0,
  output S1,
  output S2,
  output S3,
  output S4,
  output S5
);

  wire and_1_out, and_2_out, and_3_out, and_4_out;

  and and_1 (and_1_out, E0, E1);
  and and_2 (and_2_out, E2, E3);
  and and_3 (and_3_out, E4, E5);
  and and_4 (and_4_out, and_1_out, and_2_out);
  and and_5 (S0, and_4_out, and_3_out);

  assign S1 = 1'b0;
  assign S2 = 1'b0;
  assign S3 = 1'b0;
  assign S4 = 1'b0;
  assign S5 = 1'b0;
endmodule
