// Digital circuit Full Subtrator.dig as structural Verilog
module Full_Subtrator (
  input  A,
  input  B,
  input  E_in,
  output S,
  output PE
);

  wire and_1_out, and_2_out, and_3_out, not_1_out, not_2_out, xor_1_out;

  xor xor_1 (xor_1_out, A, B);
  and and_1 (and_1_out, not_1_out, B);
  not not_1 (not_1_out, A);
  and and_2 (and_2_out, not_2_out, E_in);
  not not_2 (not_2_out, A);
  and and_3 (and_3_out, B, E_in);
  xor xor_2 (S, xor_1_out, E_in);
  or or_1 (PE, and_1_out, and_2_out, and_3_out);
endmodule
