// Digital circuit Half Subtrator.dig as structural Verilog
module Half_Subtrator (
  input  A,
  input  B,
  output S,
  output Cout
);

  wire not_1_out;

  xor xor_1 (S, A, B);
  not not_1 (not_1_out, A);
  and and_1 (Cout, not_1_out, B);
endmodule
