// Digital circuit MUX.dig as structural Verilog
module MUX (
  input  Y,
  input  X,
  output _00,
  output _01,
  output _10,
  output _11
);

  and and_1 (_00, ~Y, ~X);  // And
  and and_2 (_01, Y, ~X);  // And
  and and_3 (_10, ~Y, X);  // And
  and and_4 (_11, Y, X);
endmodule
