// Digital circuit Multiplicador.dig as structural Verilog
module Multiplicador (
  input  A0,
  input  A1,
  input  A2,
  input  A3,
  input  A4,
  input  A5,
  input  B5,
  input  B4,
  input  B3,
  input  B2,
  input  B1,
  input  B0,
  output C0,
  output C1,
  output C2,
  output C3,
  output C4,
  output C5,
  output C6,
  output C7,
  output F
);

  wire \multiplicação_simples_2_ab , \multiplicação_simples_3_ab , \multiplicação_simples_4_ab ,
       \multiplicação_simples_5_ab , \multiplicação_simples_6_ab , \multiplicação_simples_7_ab ,
       \multiplicação_simples_8_ab , \multiplicação_simples_9_ab , \multiplicação_simples_10_ab ,
       \multiplicação_simples_11_ab , \multiplicação_simples_12_ab , \multiplicação_simples_13_ab ,
       \multiplicação_simples_14_ab , \multiplicação_simples_15_ab , \multiplicação_simples_16_ab ,
       somador_das_linhas_1_s0, somador_das_linhas_1_s1, somador_das_linhas_1_s2, somador_das_linhas_1_s3,
       somador_das_linhas_1_s4, somador_das_linhas_2_s0, somador_das_linhas_2_s1, somador_das_linhas_2_s2,
       somador_das_linhas_2_s3, somador_das_linhas_2_s4;

  \OverFLowMultiplicação  \overflowmultiplicação_1  (.A5(A5), .A4(A4), .B4(B4), .B5(B5), .F(F));
  \Multiplicação_Simples  \multiplicação_simples_1  (.A(A0), .B(B0), .AB(C0));
  \Multiplicação_Simples  \multiplicação_simples_2  (.A(A1), .B(B0), .AB(\multiplicação_simples_2_ab ));
  \Multiplicação_Simples  \multiplicação_simples_3  (.A(A2), .B(B0), .AB(\multiplicação_simples_3_ab ));
  \Multiplicação_Simples  \multiplicação_simples_4  (.A(A3), .B(B0), .AB(\multiplicação_simples_4_ab ));
  \Multiplicação_Simples  \multiplicação_simples_5  (.A(A0), .B(B2), .AB(\multiplicação_simples_5_ab ));
  \Multiplicação_Simples  \multiplicação_simples_6  (.A(A1), .B(B2), .AB(\multiplicação_simples_6_ab ));
  \Multiplicação_Simples  \multiplicação_simples_7  (.A(A2), .B(B2), .AB(\multiplicação_simples_7_ab ));
  \Multiplicação_Simples  \multiplicação_simples_8  (.A(A3), .B(B2), .AB(\multiplicação_simples_8_ab ));
  Somador_das_LInhas somador_das_linhas_1 (
    .A0(\multiplicação_simples_2_ab ), .A1(\multiplicação_simples_3_ab ), .A2(\multiplicação_simples_4_ab ),
    .B2(\multiplicação_simples_11_ab ), .B1(\multiplicação_simples_10_ab ),
    .B0(\multiplicação_simples_9_ab ), .B3(\multiplicação_simples_12_ab ), .s0(somador_das_linhas_1_s0),
    .s1(somador_das_linhas_1_s1), .s2(somador_das_linhas_1_s2), .s3(somador_das_linhas_1_s3),
    .s4(somador_das_linhas_1_s4));
  Somador_das_LInhas somador_das_linhas_2 (
    .A0(\multiplicação_simples_6_ab ), .A1(\multiplicação_simples_7_ab ), .A2(\multiplicação_simples_8_ab ),
    .B2(\multiplicação_simples_15_ab ), .B1(\multiplicação_simples_14_ab ),
    .B0(\multiplicação_simples_13_ab ), .B3(\multiplicação_simples_16_ab ), .s0(somador_das_linhas_2_s0),
    .s1(somador_das_linhas_2_s1), .s2(somador_das_linhas_2_s2), .s3(somador_das_linhas_2_s3),
    .s4(somador_das_linhas_2_s4));
  \Multiplicação_Simples  \multiplicação_simples_9  (.A(A0), .B(B1), .AB(\multiplicação_simples_9_ab ));
  \Multiplicação_Simples  \multiplicação_simples_10  (.A(A1), .B(B1), .AB(\multiplicação_simples_10_ab ));
  \Multiplicação_Simples  \multiplicação_simples_11  (.A(A2), .B(B1), .AB(\multiplicação_simples_11_ab ));
  \Multiplicação_Simples  \multiplicação_simples_12  (.A(A3), .B(B1), .AB(\multiplicação_simples_12_ab ));
  \Multiplicação_Simples  \multiplicação_simples_13  (.A(A0), .B(B3), .AB(\multiplicação_simples_13_ab ));
  \Multiplicação_Simples  \multiplicação_simples_14  (.A(A1), .B(B3), .AB(\multiplicação_simples_14_ab ));
  \Multiplicação_Simples  \multiplicação_simples_15  (.A(A2), .B(B3), .AB(\multiplicação_simples_15_ab ));
  \Multiplicação_Simples  \multiplicação_simples_16  (.A(A3), .B(B3), .AB(\multiplicação_simples_16_ab ));
  \Somador_da_Multiplicação__4_linhas  \somador_da_multiplicação__4_linhas_1  (
    .A0(somador_das_linhas_1_s0), .A1(somador_das_linhas_1_s1), .A2(somador_das_linhas_1_s2),
    .A3(somador_das_linhas_1_s3), .A4(somador_das_linhas_1_s4), .B1(\multiplicação_simples_5_ab ),
    .B2(somador_das_linhas_2_s0), .B3(somador_das_linhas_2_s1), .B4(somador_das_linhas_2_s2),
    .B5(somador_das_linhas_2_s3), .B6(somador_das_linhas_2_s4), .s0(C1), .s1(C2), .s2(C3), .s3(C4), .s4(C5),
    .s5(C6), .s6(C7));
endmodule
