// Digital circuit Mux da Mult.dig as structural Verilog
module Mux_da_Mult (
  input  \SO_Multiplicação ,
  input  _00,
  input  _10,
  output S0
);

  and and_1 (S0, \SO_Multiplicação , _00, _10);
endmodule
