// Digital circuit Mux das Contas.dig as structural Verilog
module Mux_das_Contas (
  input  S0_soma,
  input  \SO_Subtração ,
  input  \S0_Comparação ,
  input  \SO_Multiplicação ,
  input  _00,
  input  _10,
  output S0
);

  wire and_1_out, and_2_out, and_3_out, and_4_out, or_1_out, or_3_out;

  and and_1 (and_1_out, S0_soma, ~_00, ~_10);  // And
  or or_1 (or_1_out, and_2_out, and_1_out);
  and and_2 (and_2_out, \S0_Comparação , ~_00, _10);  // And
  or or_2 (S0, or_3_out, or_1_out);
  and and_3 (and_3_out, \SO_Subtração , _00, ~_10);  // And
  and and_4 (and_4_out, \SO_Multiplicação , _00, _10);
  or or_3 (or_3_out, and_4_out, and_3_out);
endmodule
