// Digital circuit Mux de 6 bits.dig as structural Verilog
module Mux_de_6_bits (
  input  F_Som,
  input  _00,
  input  _01,
  input  S0_Som,
  input  S1_Som,
  input  S2_Som,
  input  S3_Som,
  input  S4_Som,
  input  S5_Som,
  input  S0_Sub,
  input  S1_Sub,
  input  S2_Sub,
  input  S3_Sub,
  input  S4_Sub,
  input  S5_Sub,
  input  F_Sub,
  input  S0_Com,
  input  S1_Com,
  input  S2_Com,
  input  S3_Com,
  input  S4_Com,
  input  S5_Com,
  input  S0_Mul,
  input  S1_Mul,
  input  S2_Mul,
  input  S3_Mul,
  input  S4_Mul,
  input  S5_Mul,
  input  S6_Mul,
  input  S7_Mul,
  input  F_Mul,
  output S0,
  output S1,
  output S2,
  output S3,
  output S4,
  output S5,
  output S6,
  output S7,
  output F
);

  Mux_de_Overflow mux_de_overflow_1 (
    .S0_soma(F_Som), .\SO_Subtração (F_Sub), .\SO_Multiplicação (F_Mul), ._00(_00), ._10(_01), .S1(F));
  Mux_da_Mult mux_da_mult_1 (.\SO_Multiplicação (S7_Mul), ._00(_00), ._10(_01), .S0(S7));
  Mux_da_Mult mux_da_mult_2 (.\SO_Multiplicação (S6_Mul), ._00(_00), ._10(_01), .S0(S6));
  Mux_das_Contas mux_das_contas_1 (
    .S0_soma(S5_Som), .\SO_Subtração (S5_Sub), .\S0_Comparação (S5_Com), .\SO_Multiplicação (S5_Mul),
    ._00(_00), ._10(_01), .S0(S5));
  Mux_das_Contas mux_das_contas_2 (
    .S0_soma(S4_Som), .\SO_Subtração (S4_Sub), .\S0_Comparação (S4_Com), .\SO_Multiplicação (S4_Mul),
    ._00(_00), ._10(_01), .S0(S4));
  Mux_das_Contas mux_das_contas_3 (
    .S0_soma(S3_Som), .\SO_Subtração (S3_Sub), .\S0_Comparação (S3_Com), .\SO_Multiplicação (S3_Mul),
    ._00(_00), ._10(_01), .S0(S3));
  Mux_das_Contas mux_das_contas_4 (
    .S0_soma(S2_Som), .\SO_Subtração (S2_Sub), .\S0_Comparação (S2_Com), .\SO_Multiplicação (S2_Mul),
    ._00(_00), ._10(_01), .S0(S2));
  Mux_das_Contas mux_das_contas_5 (
    .S0_soma(S1_Som), .\SO_Subtração (S1_Sub), .\S0_Comparação (S1_Com), .\SO_Multiplicação (S1_Mul),
    ._00(_00), ._10(_01), .S0(S1));
  Mux_das_Contas mux_das_contas_6 (
    .S0_soma(S0_Som), .\SO_Subtração (S0_Sub), .\S0_Comparação (S0_Com), .\SO_Multiplicação (S0_Mul),
    ._00(_00), ._10(_01), .S0(S0));
endmodule
