// Digital circuit OverFLowMultiplicação.dig as structural Verilog
module \OverFLowMultiplicação  (
  input  A5,
  input  A4,
  input  B4,
  input  B5,
  output F
);

  wire and_1_out, and_2_out;

  and and_1 (and_1_out, ~A4, ~A5);  // And
  and and_2 (and_2_out, ~B4, ~B5);  // And
  or or_1 (F, ~and_1_out, ~and_2_out);  // Or
endmodule
