// Digital circuit OverflowSubtração.dig as structural Verilog
module \OverflowSubtração  (
  input  S5,
  input  A5,
  input  PE,
  input  B5,
  output F
);

  wire and_1_out, and_2_out, or_1_out;

  and and_1 (and_1_out, A5, B5, ~S5);  // And
  and and_2 (and_2_out, ~A5, ~B5, S5);  // And
  or or_1 (or_1_out, and_1_out, and_2_out);
  or or_2 (F, or_1_out, ~PE);  // Or
endmodule
