// Digital circuit Somador da Multiplicação (4 linhas).dig as structural Verilog
module \Somador_da_Multiplicação__4_linhas  (
  input  A0,
  input  A1,
  input  A2,
  input  A3,
  input  A4,
  input  B1,
  input  B2,
  input  B3,
  input  B4,
  input  B5,
  input  B6,
  output s0,
  output s1,
  output s2,
  output s3,
  output s4,
  output s5,
  output s6
);

  wire full_adder_1_cout, full_adder_2_cout, full_adder_3_cout, half_adder_1_cout, half_adder_2_cout;

  Half_Adder half_adder_1 (.A(A1), .B(B1), .S(s1), .Cout(half_adder_1_cout));
  Full_Adder full_adder_1 (.A(A2), .B(B2), .Cin(half_adder_1_cout), .S(s2), .Cout(full_adder_1_cout));
  Full_Adder full_adder_2 (.A(A3), .B(B3), .Cin(full_adder_1_cout), .S(s3), .Cout(full_adder_2_cout));
  Full_Adder full_adder_3 (.A(A4), .B(B4), .Cin(full_adder_2_cout), .S(s4), .Cout(full_adder_3_cout));
  Half_Adder half_adder_2 (.A(full_adder_3_cout), .B(B5), .S(s5), .Cout(half_adder_2_cout));
  Half_Adder half_adder_3 (.A(half_adder_2_cout), .B(B6), .S(s6));  // open: Cout

  assign s0 = A0;
endmodule
