// Digital circuit Somador das LInhas.dig as structural Verilog
module Somador_das_LInhas (
  input  A0,
  input  A1,
  input  A2,
  input  B2,
  input  B1,
  input  B0,
  input  B3,
  output s0,
  output s1,
  output s2,
  output s3,
  output s4
);

  wire full_adder_1_cout, full_adder_2_cout, half_adder_1_cout;

  Half_Adder half_adder_1 (.A(A0), .B(B0), .S(s0), .Cout(half_adder_1_cout));
  Half_Adder half_adder_2 (.A(B3), .B(full_adder_2_cout), .S(s3), .Cout(s4));
  Full_Adder full_adder_1 (.A(A1), .B(B1), .Cin(half_adder_1_cout), .S(s1), .Cout(full_adder_1_cout));
  Full_Adder full_adder_2 (.A(A2), .B(B2), .Cin(full_adder_1_cout), .S(s2), .Cout(full_adder_2_cout));
endmodule
