// Digital circuit Somador do Complemento de 2.dig as structural Verilog
module Somador_do_Complemento_de_2 (
  input  B0,
  input  B1,
  input  B2,
  input  B3,
  input  B4,
  input  B5,
  output s0,
  output s1,
  output s2,
  output s3,
  output s4,
  output s5
);

  wire half_adder_1_cout, half_adder_2_cout, half_adder_3_cout, half_adder_4_cout, half_adder_5_cout;

  Half_Adder half_adder_1 (.A(1'b1), .B(B0), .S(s0), .Cout(half_adder_1_cout));
  Half_Adder half_adder_2 (.A(half_adder_1_cout), .B(B1), .S(s1), .Cout(half_adder_2_cout));
  Half_Adder half_adder_3 (.A(half_adder_2_cout), .B(B2), .S(s2), .Cout(half_adder_3_cout));
  Half_Adder half_adder_4 (.A(half_adder_3_cout), .B(B3), .S(s3), .Cout(half_adder_4_cout));
  Half_Adder half_adder_5 (.A(half_adder_4_cout), .B(B4), .S(s4), .Cout(half_adder_5_cout));
  Half_Adder half_adder_6 (.A(half_adder_5_cout), .B(B5), .S(s5));  // open: Cout
endmodule
