// Digital circuit main.dig as structural Verilog
module main (
  input  B3,
  input  B2,
  input  B1,
  input  B0,
  input  O0,
  input  A3,
  input  A2,
  input  A1,
  input  A0,
  input  O1,
  input  A4,
  input  A5,
  input  B4,
  input  B5,
  output F,
  output s7,
  output s6,
  output s5,
  output s4,
  output s3,
  output s2,
  output s1,
  output s0
);

  Circuito circuito_1 (
    .A5(B5), .A4(B4), .A3(B3), .A2(B2), .A1(B1), .A0(B0), .O1(O1), .O0(O0), .B5(A5), .B4(A4), .B3(A3),
    .B2(A2), .B1(A1), .B0(A0), .F(F), .s7(s7), .s6(s6), .s5(s5), .s4(s4), .s3(s3), .s2(s2), .s1(s1), .s0(s0));
endmodule
